# Fritzing sketch 회로도 (saved by Fritzing 1.0.5)
breadboards: 1

parts:
  J1 = STM32 Nucleo boards
  M1 = RioRand LM2596
  부품2 = InvenSense MPU6050
  부품4 = Motor Driver 1A Dual TB6612FNG_DFROBOT
  M2 = DC Motor [voltage_(max)=6V voltage_(min)=3V]
  M3 = DC Motor [voltage_(max)=6V voltage_(min)=3V]
  V1 = DC Power Supply [voltage=12V internal_resistance=1Ω max_current=0.1A]

nets:
  N1: J1.CN_01, J1.CN_02
  N2: J1.CN_03, J1.CN_04
  N3: J1.JP5_1, J1.JP5_2
  N4: J1.GND#880, J1.GND#881
  N5: J1.GND#1149, J1.GND#1150
  3V3: J1.3V3, 부품4.VCC
  5V: J1.5V, 부품2.VCC
  GND: J1.GND#1188, M1.Pin_2, 부품2.GND, 부품4.GND, V1.Pin_1
  N6: J1.GND#1189, M1.Pin_4
  N7: J1.VIN, M1.Pin_3
  N8: J1.PB8, 부품2.SCL
  N9: J1.PB9, 부품2.SDA
  N10: J1.PA0, 부품4.PWM1
  N11: J1.PA1, 부품4.PWM2
  N12: J1.PC1, 부품4.DIR2
  N13: J1.PC0, 부품4.DIR1
  N14: M1.Pin_1, 부품4.VM, V1.Pin_2
  N15: 부품4.M1+, M2.pin_2
  N16: 부품4.M1-, M2.pin_1
  N17: 부품4.M2+, M3.pin_2
  N18: 부품4.M2-, M3.pin_1

custom parts:
  Motor Driver 1A Dual TB6612FNG_DFROBOT: The TB6612FNG motor driver can control up to two DC motors at a constant current of 1.2A (3.2A peak). Two input signals (IN1 and IN2) can be used to control the motor in one of four function modes - CW, CCW, short-brake, and stop. The two motor outputs (A and B) can be separately controlled, the speed of each motor is controlled via a PWM input signal with a frequency up to 100kHz. The STBY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
